# Fritzing sketch Current_sensor (saved by Fritzing 0.9.3b)
breadboards: 1

parts:
  Componente1 = Arduino Nano (Rev3.0)
  PSU1 = Adjustable Breadboard Power Supply
  U1 = LM358 [package=dip08]
  R1 = Resistor [tolerance=±5% resistance=1k package=THT]
  R2 = Resistor [tolerance=±1% resistance=3.8k package=THT]
  L1 = Inductor [package="0805 [SMD]"]

nets:
  N1: Componente1.GND, PSU1.Vout+, PSU1.Vin-, R1.Pin_0, L1.pin_1
  N2: Componente1.A0, U1.G$1_OUT, R2.Pin_1
  N3: PSU1.Vout-, U1.G$1_V-
  N4: PSU1.Vin+, U1.G$1_V+
  N5: U1.G$1_-IN, R1.Pin_1, R2.Pin_0
  N6: U1.G$1_+IN, L1.pin_0

// code stored in the sketch: main.ino
/*
SCT-013 Current sensor reader

Lee la señal analógica A0:

	* SCT-013-50 -> 50A @ 1V
		- Con 3 vueltas es capaz de leer 16.67A
		- Con la señal pasando por un amplificador no inversor G=4.8 es capaz de recibir hasta 4.8V

	* Señal de entrada 16.67 A @ 4.8v
		-  P = V * I ;  P = 3.834 kW
			 # Resolucion (potencia) =  P / (2^10-1) ; Resolucion = 3.75 W
			# Resolucion  (corriente) = 16.67 /  (2^10-1) ; Resolucion = 16mA
*/

float current, power = 0;
 int SCT_raw = 0;

void setup() {
  Serial.begin(9600);
}

void loop() {
	SCT_raw = analogRead(A0);
    current = SCT_raw*0.01629;
    power = current * 230;

  Serial.println(current, power);
  delay(1000);
}
